// Logisim project CPU-8Ins-Jr-Lh-Sb-J.circ as structural Verilog: 14 circuits, main circuit main
module main (
  input  Reset,
  output [31:0] out_2,
  output out_3,
  output [4:0] out_4,
  output [31:0] out_5,
  output out_6,
  output [4:0] out_7,
  output [31:0] out_8
);

  wire A_B, AluSrc, and_2_out, Branch, Byte, Controller_regwrite, ExtendType, HalfWord, J, J_L, Jr, MemToReg,
       or_1_out, RegDst, Shift_16bit;
  wire [1:0] Address_Byte;
  wire [2:0] ALU_Op;
  wire [3:0] ALU_Control_alu_ctr;
  wire [4:0] multiplexer_14_out;
  wire [7:0] multiplexer_9_out;
  wire [15:0] multiplexer_8_out;
  wire [31:0] bit_extender_1_out, bit_extender_2_out, DM_ALU_Result, Extend_Immediate, IFU_pc_now, MemValue,
       multiplexer_2_out, multiplexer_3_out, multiplexer_4_out, multiplexer_5_out, multiplexer_7_out,
       multiplexer_10_out, multiplexer_11_out, n32bit_adder_1_out_3, n32bit_adder_2_out_3, PC_4, PC_Next,
       PC_Now, Rs_Data, Rt_Data, shifter_1_out, shifter_2_out;
  wire [31:7] ALU_Result;

  _32bit_Adder u_32bit_adder_1 (.A(32'h3000), .B(PC_Next), .out_3(n32bit_adder_1_out_3));
  _32bit_Subber u_32bit_subber_1 (.A(IFU_pc_now), .B(32'h3000), .out_3(PC_Now));
  IFU IFU (.PC_next(n32bit_adder_1_out_3), .Reset(Reset), .PC_now(IFU_pc_now), .Instruction(out_2));
  Controller Controller (
    .Op(out_2[31:26]), .MemWrite(out_6), .RegWrite(Controller_regwrite), .MemToReg(MemToReg),
    .ExtendType(ExtendType), .AluSrc(AluSrc), .RegDst(RegDst), .Branch(Branch), .ALU_Op(ALU_Op),
    .Shift_16bit(Shift_16bit), .J_L(J_L), .HalfWord(HalfWord), .Byte(Byte), .J(J));
  and and_1 (out_3, Controller_regwrite, ~Jr);  // AND_Gate
  Multiplexer #(.width(32)) multiplexer_1 (.in0(DM_ALU_Result), .in1(PC_4), .out(out_5), .sel(J_L));  // open: en
  GRF GRF (
    .RS(out_2[25:21]), .RT(out_2[20:16]), .RD(out_2[15:11]), .Input(out_5), .RegWrite(out_3),
    .RegDst(RegDst), .Reset(Reset), .J_L(J_L), .RS_data(Rs_Data), .RT_data(Rt_Data));
  Extender Extender (.Immediate(out_2[15:0]), .ExtendType(ExtendType), .Output(Extend_Immediate));
  _32bit_Adder Add_4bit (.A(PC_Now), .B(32'h4), .out_3(PC_4));
  Shifter #(.width(32)) shifter_1 (.in(Extend_Immediate), .\dist (5'b00010), .out(shifter_1_out));
  Multiplexer #(.width(32)) multiplexer_2 (
    .in0(Extend_Immediate), .in1(shifter_2_out), .out(multiplexer_2_out), .sel(Shift_16bit));  // open: en
  Shifter #(.width(32)) shifter_2 (.in(Extend_Immediate), .\dist (5'b10000), .out(shifter_2_out));
  _32bit_Adder u_32bit_adder_2 (.A(PC_4), .B(shifter_1_out), .out_3(n32bit_adder_2_out_3));
  and and_2 (and_2_out, A_B, Branch);
  Multiplexer #(.width(32)) multiplexer_3 (
    .in0(Rt_Data), .in1(multiplexer_2_out), .out(multiplexer_3_out), .sel(AluSrc));  // open: en
  Multiplexer #(.width(32)) multiplexer_4 (
    .in0(PC_4), .in1(n32bit_adder_2_out_3), .out(multiplexer_4_out), .sel(and_2_out));  // open: en
  ALU ALU (
    .Rs_Data(Rs_Data), .Rt_Data_Immediate(multiplexer_3_out), .ALU_Ctr(ALU_Control_alu_ctr),
    .Result({ALU_Result, out_7, Address_Byte}), .A_B(A_B));
  ALU_Control ALU_Control (.ALU_Op(ALU_Op), .Func(out_2[5:0]), .ALU_Ctr(ALU_Control_alu_ctr), .Jr(Jr));
  Multiplexer #(.width(32)) multiplexer_5 (
    .in0(multiplexer_4_out), .in1({PC_Now[31:28], out_2[25:0], 2'b00}), .out(multiplexer_5_out),
    .sel(or_1_out));  // open: en
  or or_1 (or_1_out, J_L, J);
  Multiplexer #(.width(32)) multiplexer_6 (
    .in0(multiplexer_5_out), .in1(Rs_Data), .out(PC_Next), .sel(Jr));  // open: en
  Multiplexer #(.width(32)) multiplexer_7 (
    .in0({ALU_Result, out_7, Address_Byte}), .in1(MemValue), .out(multiplexer_7_out), .sel(MemToReg));  // open: en
  Multiplexer #(.width(16)) multiplexer_8 (
    .in0(multiplexer_7_out[15:0]), .in1(multiplexer_7_out[31:16]), .out(multiplexer_8_out),
    .sel(Address_Byte[1]));  // open: en
  Multiplexer #(.select(2), .width(8)) multiplexer_9 (
    .in0(multiplexer_7_out[7:0]), .in1(multiplexer_7_out[15:8]), .in2(multiplexer_7_out[23:16]),
    .in3(multiplexer_7_out[31:24]), .out(multiplexer_9_out), .sel(Address_Byte));  // open: en
  assign bit_extender_1_out = {{16{multiplexer_8_out[15]}}, multiplexer_8_out};  // Bit_Extender bit_extender_1
  assign bit_extender_2_out = {{24{multiplexer_9_out[7]}}, multiplexer_9_out};  // Bit_Extender bit_extender_2
  Multiplexer #(.select(2), .width(32)) multiplexer_10 (
    .in0({MemValue[31:8], Rt_Data[7:0]}), .in1({MemValue[31:16], Rt_Data[7:0], MemValue[7:0]}),
    .in2({MemValue[31:24], Rt_Data[7:0], MemValue[15:0]}), .in3({Rt_Data[7:0], MemValue[23:0]}),
    .out(multiplexer_10_out), .sel(Address_Byte));  // open: en
  Multiplexer #(.width(32)) multiplexer_11 (
    .in0(multiplexer_7_out), .in1(bit_extender_1_out), .out(multiplexer_11_out), .sel(HalfWord));  // open: en
  Multiplexer #(.width(32)) multiplexer_12 (
    .in0(Rt_Data), .in1(multiplexer_10_out), .out(out_8), .sel(Byte));  // open: en
  Multiplexer #(.width(32)) multiplexer_13 (
    .in0(multiplexer_11_out), .in1(bit_extender_2_out), .out(DM_ALU_Result), .sel(Byte));  // open: en
  DM DM (
    .Address({ALU_Result, out_7, Address_Byte}), .Data(out_8), .mem_write(out_6), .Reset(Reset),
    .Data_2(MemValue));
  Multiplexer #(.width(5)) multiplexer_14 (
    .in0(out_2[20:16]), .in1(out_2[15:11]), .out(multiplexer_14_out), .sel(RegDst));  // open: en
  Multiplexer #(.width(5)) multiplexer_15 (
    .in0(multiplexer_14_out), .in1({5{1'b1}}), .out(out_4), .sel(J_L));  // open: en

  // Other names for the same wires on the sheet: Func[5:0] = out_2[5:0]; Immediate[15:0] = out_2[15:0];
  //   Instr[31:0] = out_2; Jump_Offset[25:0] = out_2[25:0]; SHAMT[4:0] = out_2[10:6]; RD[4:0] = out_2[15:11];
  //   RT[4:0] = out_2[20:16]; RS_BASE[4:0] = out_2[25:21]; ALU_Result[6:0] = {out_7, Address_Byte};
  //   Address_HW = Address_Byte[1]; DM_Input[31:0] = out_8; MemWrite = out_6; Op[5:0] = out_2[31:26];
  //   RegInput[31:0] = out_5; RegWrite = out_3

  // Notes on the sheet:
  //   Func
  //   SHAMT
  //   RD
  //   RT
  //   RS/BASE
  //   Op
  //   datain
  //   0低16位 1高16位
endmodule

// PC
module IFU (
  input  [31:0] PC_next,
  input  Reset,
  output [31:0] PC_now,
  output [31:0] Instruction
);

  wire clock_1_out;

  Clock clock_1 (.out(clock_1_out));
  Register #(.width(32)) PC_reg (.D(PC_next), .Q(PC_now), .clk(clock_1_out), .clr(Reset));  // open: en
  ROM #(.addrWidth(5), .dataWidth(32)) rom_1 (.addr(PC_now[6:2]), .data(Instruction));  // open: sel

  // Notes on the sheet:
  //   contents of rom_1 (hex, n*v repeats v):
  //   37bd0100 3c1d0000 35080001 3c080000 35290005 3c090000 c000008 8000016 36f70008 3c170000 3b7e823
  //   afbf0000 afb00004 2088021 12090001 c000008 8fbf0000 8fb00004 36f70008 3c170000 3b7e821 3e00008
endmodule

module GRF (
  input  [4:0] RS,
  input  [4:0] RT,
  input  [4:0] RD,
  input  [31:0] Input,
  input  RegWrite,
  input  RegDst,
  input  Reset,
  input  J_L,
  output [31:0] RS_data,
  output [31:0] RT_data
);

  wire and_1_out, and_2_out, and_3_out, and_4_out, and_5_out, and_6_out, and_7_out, and_8_out, and_9_out,
       and_10_out, and_11_out, and_12_out, and_13_out, and_14_out, and_15_out, and_16_out, and_17_out,
       and_18_out, and_19_out, and_20_out, and_21_out, and_22_out, and_23_out, and_24_out, and_25_out,
       and_26_out, and_27_out, and_28_out, and_29_out, and_30_out, and_31_out, and_32_out, clock_1_out,
       decoder_1_out0, decoder_1_out1, decoder_1_out2, decoder_1_out3, decoder_1_out4, decoder_1_out5,
       decoder_1_out6, decoder_1_out7, decoder_1_out8, decoder_1_out9, decoder_1_out10, decoder_1_out11,
       decoder_1_out12, decoder_1_out13, decoder_1_out14, decoder_1_out15, decoder_1_out16, decoder_1_out17,
       decoder_1_out18, decoder_1_out19, decoder_1_out20, decoder_1_out21, decoder_1_out22, decoder_1_out23,
       decoder_1_out24, decoder_1_out25, decoder_1_out26, decoder_1_out27, decoder_1_out28, decoder_1_out29,
       decoder_1_out30, decoder_1_out31;
  wire [4:0] multiplexer_1_out, multiplexer_2_out;
  wire [31:0] _0_q, _1_q, _2_q, _3_q, _4_q, _5_q, _6_q, _7_q, _8_q, _9_q, _10_q, _11_q, _12_q, _13_q, _14_q,
       _15_q, _16_q, _17_q, _18_q, _19_q, _20_q, _21_q, _22_q, _23_q, _24_q, _25_q, _26_q, _27_q, _28_q,
       _29_q, _30_q, _31_q;

  Multiplexer #(.width(5)) multiplexer_1 (.in0(RT), .in1(RD), .out(multiplexer_1_out), .sel(RegDst));  // open: en
  Multiplexer #(.width(5)) multiplexer_2 (
    .in0(multiplexer_1_out), .in1({5{1'b1}}), .out(multiplexer_2_out), .sel(J_L));  // open: en
  Decoder #(.select(5)) decoder_1 (
    .out0(decoder_1_out0), .out1(decoder_1_out1), .out2(decoder_1_out2), .out3(decoder_1_out3),
    .out4(decoder_1_out4), .out5(decoder_1_out5), .out6(decoder_1_out6), .out7(decoder_1_out7),
    .out8(decoder_1_out8), .out9(decoder_1_out9), .out10(decoder_1_out10), .out11(decoder_1_out11),
    .out12(decoder_1_out12), .out13(decoder_1_out13), .out14(decoder_1_out14), .out15(decoder_1_out15),
    .out16(decoder_1_out16), .out17(decoder_1_out17), .out18(decoder_1_out18), .out19(decoder_1_out19),
    .out20(decoder_1_out20), .out21(decoder_1_out21), .out22(decoder_1_out22), .out23(decoder_1_out23),
    .out24(decoder_1_out24), .out25(decoder_1_out25), .out26(decoder_1_out26), .out27(decoder_1_out27),
    .out28(decoder_1_out28), .out29(decoder_1_out29), .out30(decoder_1_out30), .out31(decoder_1_out31),
    .sel(multiplexer_2_out));  // open: en
  and and_1 (and_1_out, decoder_1_out0, RegWrite);
  and and_2 (and_2_out, decoder_1_out1, RegWrite);
  and and_3 (and_3_out, decoder_1_out2, RegWrite);
  and and_4 (and_4_out, decoder_1_out3, RegWrite);
  and and_5 (and_5_out, decoder_1_out4, RegWrite);
  and and_6 (and_6_out, decoder_1_out5, RegWrite);
  and and_7 (and_7_out, decoder_1_out6, RegWrite);
  and and_8 (and_8_out, decoder_1_out7, RegWrite);
  and and_9 (and_9_out, decoder_1_out8, RegWrite);
  and and_10 (and_10_out, decoder_1_out9, RegWrite);
  and and_11 (and_11_out, decoder_1_out10, RegWrite);
  and and_12 (and_12_out, decoder_1_out11, RegWrite);
  and and_13 (and_13_out, decoder_1_out12, RegWrite);
  and and_14 (and_14_out, decoder_1_out13, RegWrite);
  and and_15 (and_15_out, decoder_1_out14, RegWrite);
  and and_16 (and_16_out, decoder_1_out15, RegWrite);
  and and_17 (and_17_out, decoder_1_out16, RegWrite);
  and and_18 (and_18_out, decoder_1_out17, RegWrite);
  and and_19 (and_19_out, decoder_1_out18, RegWrite);
  and and_20 (and_20_out, decoder_1_out19, RegWrite);
  and and_21 (and_21_out, decoder_1_out20, RegWrite);
  and and_22 (and_22_out, decoder_1_out21, RegWrite);
  and and_23 (and_23_out, decoder_1_out22, RegWrite);
  and and_24 (and_24_out, decoder_1_out23, RegWrite);
  and and_25 (and_25_out, decoder_1_out24, RegWrite);
  and and_26 (and_26_out, decoder_1_out25, RegWrite);
  and and_27 (and_27_out, decoder_1_out26, RegWrite);
  and and_28 (and_28_out, decoder_1_out27, RegWrite);
  and and_29 (and_29_out, decoder_1_out28, RegWrite);
  and and_30 (and_30_out, decoder_1_out29, RegWrite);
  and and_31 (and_31_out, decoder_1_out30, RegWrite);
  and and_32 (and_32_out, decoder_1_out31, RegWrite);
  Clock clock_1 (.out(clock_1_out));
  Register #(.width(32)) _0 (.D({32{1'b0}}), .en(and_1_out), .Q(_0_q), .clk(clock_1_out), .clr(Reset));
  Register #(.width(32)) _1 (.D(Input), .en(and_2_out), .Q(_1_q), .clk(clock_1_out), .clr(Reset));
  Register #(.width(32)) _2 (.D(Input), .en(and_3_out), .Q(_2_q), .clk(clock_1_out), .clr(Reset));
  Register #(.width(32)) _3 (.D(Input), .en(and_4_out), .Q(_3_q), .clk(clock_1_out), .clr(Reset));
  Register #(.width(32)) _4 (.D(Input), .en(and_5_out), .Q(_4_q), .clk(clock_1_out), .clr(Reset));
  Register #(.width(32)) _5 (.D(Input), .en(and_6_out), .Q(_5_q), .clk(clock_1_out), .clr(Reset));
  Register #(.width(32)) _6 (.D(Input), .en(and_7_out), .Q(_6_q), .clk(clock_1_out), .clr(Reset));
  Register #(.width(32)) _7 (.D(Input), .en(and_8_out), .Q(_7_q), .clk(clock_1_out), .clr(Reset));
  Register #(.width(32)) _8 (.D(Input), .en(and_9_out), .Q(_8_q), .clk(clock_1_out), .clr(Reset));
  Register #(.width(32)) _9 (.D(Input), .en(and_10_out), .Q(_9_q), .clk(clock_1_out), .clr(Reset));
  Register #(.width(32)) _10 (.D(Input), .en(and_11_out), .Q(_10_q), .clk(clock_1_out), .clr(Reset));
  Register #(.width(32)) _11 (.D(Input), .en(and_12_out), .Q(_11_q), .clk(clock_1_out), .clr(Reset));
  Register #(.width(32)) _12 (.D(Input), .en(and_13_out), .Q(_12_q), .clk(clock_1_out), .clr(Reset));
  Register #(.width(32)) _13 (.D(Input), .en(and_14_out), .Q(_13_q), .clk(clock_1_out), .clr(Reset));
  Register #(.width(32)) _14 (.D(Input), .en(and_15_out), .Q(_14_q), .clk(clock_1_out), .clr(Reset));
  Register #(.width(32)) _15 (.D(Input), .en(and_16_out), .Q(_15_q), .clk(clock_1_out), .clr(Reset));
  Register #(.width(32)) _16 (.D(Input), .en(and_17_out), .Q(_16_q), .clk(clock_1_out), .clr(Reset));
  Register #(.width(32)) _17 (.D(Input), .en(and_18_out), .Q(_17_q), .clk(clock_1_out), .clr(Reset));
  Register #(.width(32)) _18 (.D(Input), .en(and_19_out), .Q(_18_q), .clk(clock_1_out), .clr(Reset));
  Register #(.width(32)) _19 (.D(Input), .en(and_20_out), .Q(_19_q), .clk(clock_1_out), .clr(Reset));
  Register #(.width(32)) _20 (.D(Input), .en(and_21_out), .Q(_20_q), .clk(clock_1_out), .clr(Reset));
  Register #(.width(32)) _21 (.D(Input), .en(and_22_out), .Q(_21_q), .clk(clock_1_out), .clr(Reset));
  Register #(.width(32)) _22 (.D(Input), .en(and_23_out), .Q(_22_q), .clk(clock_1_out), .clr(Reset));
  Register #(.width(32)) _23 (.D(Input), .en(and_24_out), .Q(_23_q), .clk(clock_1_out), .clr(Reset));
  Register #(.width(32)) _24 (.D(Input), .en(and_25_out), .Q(_24_q), .clk(clock_1_out), .clr(Reset));
  Register #(.width(32)) _25 (.D(Input), .en(and_26_out), .Q(_25_q), .clk(clock_1_out), .clr(Reset));
  Register #(.width(32)) _26 (.D(Input), .en(and_27_out), .Q(_26_q), .clk(clock_1_out), .clr(Reset));
  Register #(.width(32)) _27 (.D(Input), .en(and_28_out), .Q(_27_q), .clk(clock_1_out), .clr(Reset));
  Register #(.width(32)) _28 (.D(Input), .en(and_29_out), .Q(_28_q), .clk(clock_1_out), .clr(Reset));
  Register #(.width(32)) _29 (.D(Input), .en(and_30_out), .Q(_29_q), .clk(clock_1_out), .clr(Reset));
  Register #(.width(32)) _30 (.D(Input), .en(and_31_out), .Q(_30_q), .clk(clock_1_out), .clr(Reset));
  Register #(.width(32)) _31 (.D(Input), .en(and_32_out), .Q(_31_q), .clk(clock_1_out), .clr(Reset));
  Multiplexer #(.select(5), .width(32)) multiplexer_3 (
    .in0(_0_q), .in1(_1_q), .in2(_2_q), .in3(_3_q), .in4(_4_q), .in5(_5_q), .in6(_6_q), .in7(_7_q),
    .in8(_8_q), .in9(_9_q), .in10(_10_q), .in11(_11_q), .in12(_12_q), .in13(_13_q), .in14(_14_q),
    .in15(_15_q), .in16(_16_q), .in17(_17_q), .in18(_18_q), .in19(_19_q), .in20(_20_q), .in21(_21_q),
    .in22(_22_q), .in23(_23_q), .in24(_24_q), .in25(_25_q), .in26(_26_q), .in27(_27_q), .in28(_28_q),
    .in29(_29_q), .in30(_30_q), .in31(_31_q), .out(RS_data), .sel(RS));  // open: en
  Multiplexer #(.select(5), .width(32)) multiplexer_4 (
    .in0(_0_q), .in1(_1_q), .in2(_2_q), .in3(_3_q), .in4(_4_q), .in5(_5_q), .in6(_6_q), .in7(_7_q),
    .in8(_8_q), .in9(_9_q), .in10(_10_q), .in11(_11_q), .in12(_12_q), .in13(_13_q), .in14(_14_q),
    .in15(_15_q), .in16(_16_q), .in17(_17_q), .in18(_18_q), .in19(_19_q), .in20(_20_q), .in21(_21_q),
    .in22(_22_q), .in23(_23_q), .in24(_24_q), .in25(_25_q), .in26(_26_q), .in27(_27_q), .in28(_28_q),
    .in29(_29_q), .in30(_30_q), .in31(_31_q), .out(RT_data), .sel(RT));  // open: en
endmodule

module ALU (
  input  [31:0] Rs_Data,
  input  [31:0] Rt_Data_Immediate,
  input  [3:0] ALU_Ctr,
  output [31:0] Result,
  output A_B
);

  wire [31:0] Addu_out_3, And_out_3, Or_out_3, Subu_out_3;

  _32bit_Adder Addu (.A(Rs_Data), .B(Rt_Data_Immediate), .out_3(Addu_out_3));
  _32bit_Subber Subu (.A(Rs_Data), .B(Rt_Data_Immediate), .out_3(Subu_out_3));
  _32bit_Andder And (.A(Rs_Data), .B(Rt_Data_Immediate), .out_3(And_out_3));
  _32bit_Orer Or (.A(Rs_Data), .B(Rt_Data_Immediate), .out_3(Or_out_3));
  _32bit_Comparer Comparer (.A(Rs_Data), .B(Rt_Data_Immediate), .A_B_2(A_B));  // open: A_B, A_B_3
  Multiplexer #(.select(4), .width(32)) multiplexer_1 (
    .in0(And_out_3), .in1(Or_out_3), .in2(Addu_out_3), .in6(Subu_out_3), .out(Result), .sel(ALU_Ctr));  // open: in3, in4, in5, in7, in8, in9, in10, in11, in12, in13, in14, in15, en

  // Other names for the same wires on the sheet: Rt_Data[31:0] = Rt_Data_Immediate
endmodule

module DM (
  input  [31:0] Address,
  input  [31:0] Data,
  input  mem_write,
  input  Reset,
  output [31:0] Data_2
);

  wire clock_1_out;

  Clock clock_1 (.out(clock_1_out));
  RAM #(.addrWidth(5), .dataWidth(32), .bus("separate")) ram_1 (
    .addr(Address[6:2]), .din(Data), .data(Data_2), .str(mem_write), .clk(clock_1_out), .ld(1'b1), .clr(Reset));  // open: sel
endmodule

module Extender (
  input  [15:0] Immediate,
  input  ExtendType,
  output [31:0] Output
);

  wire [31:0] bit_extender_1_out, bit_extender_2_out;

  assign bit_extender_1_out = {{16{1'b0}}, Immediate};  // Bit_Extender bit_extender_1
  assign bit_extender_2_out = {{16{Immediate[15]}}, Immediate};  // Bit_Extender bit_extender_2
  Multiplexer #(.width(32)) multiplexer_1 (
    .in0(bit_extender_1_out), .in1(bit_extender_2_out), .out(Output), .sel(ExtendType));  // open: en
endmodule

module Controller (
  input  [5:0] Op,
  output MemWrite,
  output RegWrite,
  output MemToReg,
  output ExtendType,
  output AluSrc,
  output RegDst,
  output Branch,
  output Shift_16bit,
  output J_L,
  output HalfWord,
  output Byte,
  output J,
  output [2:0] ALU_Op
);

  wire beq, j_t, jal, lb, lh, lui, lw, not_1_out, not_2_out, not_3_out, not_4_out, not_5_out, not_6_out,
       not_7_out, not_8_out, not_9_out, not_10_out, not_11_out, not_12_out, not_13_out, not_14_out,
       not_15_out, not_16_out, not_17_out, not_18_out, not_19_out, not_20_out, not_21_out, not_22_out,
       not_23_out, not_24_out, not_25_out, not_26_out, not_27_out, not_28_out, not_29_out, not_30_out,
       not_31_out, not_32_out, not_33_out, not_34_out, not_35_out, not_36_out, not_37_out, not_38_out,
       not_39_out, not_40_out, not_41_out, not_42_out, not_43_out, ori, R, sb, sw;

  not not_1 (not_1_out, Op[2]);
  not not_2 (not_2_out, Op[3]);
  not not_3 (not_3_out, Op[4]);
  not not_4 (not_4_out, Op[5]);
  and u_R (R, not_4_out, not_3_out, not_2_out, not_1_out, not_7_out, not_6_out);
  not not_5 (not_5_out, Op[5]);
  not not_6 (not_6_out, Op[0]);
  not not_7 (not_7_out, Op[1]);
  not not_8 (not_8_out, Op[4]);
  and u_lui (lui, not_5_out, not_8_out, Op[3], Op[2], Op[1], Op[0]);
  or u_MemWrite (MemWrite, sb, sw);
  not not_9 (not_9_out, Op[4]);
  not not_10 (not_10_out, Op[3]);
  not not_11 (not_11_out, Op[2]);
  and u_lw (lw, Op[5], not_9_out, not_10_out, not_11_out, Op[1], Op[0]);
  or u_RegWrite (RegWrite, R, lw, lh, lui, ori, jal, lb);
  not not_12 (not_12_out, Op[4]);
  not not_13 (not_13_out, Op[2]);
  and u_sw (sw, Op[5], not_12_out, Op[3], not_13_out, Op[1], Op[0]);
  or u_MemToReg (MemToReg, lw, lh, lb);
  not not_14 (not_14_out, Op[5]);
  not not_15 (not_15_out, Op[4]);
  not not_16 (not_16_out, Op[1]);
  and u_ori (ori, not_14_out, not_15_out, Op[3], Op[2], not_16_out, Op[0]);
  or Extend (ExtendType, beq, lw, sw, lh, lb, sb);
  not not_17 (not_17_out, Op[5]);
  not not_18 (not_18_out, Op[0]);
  not not_19 (not_19_out, Op[4]);
  not not_20 (not_20_out, Op[3]);
  not not_21 (not_21_out, Op[1]);
  and u_beq (beq, not_17_out, not_19_out, not_20_out, Op[2], not_21_out, not_18_out);
  not not_22 (not_22_out, Op[3]);
  not not_23 (not_23_out, Op[2]);
  not not_24 (not_24_out, Op[4]);
  not not_25 (not_25_out, Op[5]);
  and u_jal (jal, not_25_out, not_24_out, not_22_out, not_23_out, Op[1], Op[0]);
  or u_AluSrc (AluSrc, sb, lw, sw, lui, ori, lh, lb);
  not not_26 (not_26_out, Op[4]);
  not not_27 (not_27_out, Op[2]);
  not not_28 (not_28_out, Op[3]);
  and u_lh (lh, Op[5], not_26_out, not_28_out, not_27_out, not_29_out, Op[0]);
  not not_29 (not_29_out, Op[1]);
  not not_30 (not_30_out, Op[3]);
  not not_31 (not_31_out, Op[4]);
  buf u_RegDst (RegDst, R);  // OR_Gate
  not not_32 (not_32_out, Op[0]);
  not not_33 (not_33_out, Op[1]);
  not not_34 (not_34_out, Op[2]);
  and u_lb (lb, Op[5], not_31_out, not_30_out, not_34_out, not_33_out, not_32_out);
  buf u_Branch (Branch, beq);  // OR_Gate
  not not_35 (not_35_out, Op[2]);
  not not_36 (not_36_out, Op[4]);
  not not_37 (not_37_out, Op[0]);
  not not_38 (not_38_out, Op[1]);
  and u_sb (sb, Op[5], not_36_out, Op[3], not_35_out, not_38_out, not_37_out);
  not not_39 (not_39_out, Op[4]);
  not not_40 (not_40_out, Op[5]);
  not not_41 (not_41_out, Op[2]);
  not not_42 (not_42_out, Op[3]);
  and u_j (j_t, not_40_out, not_39_out, not_42_out, not_41_out, Op[1], not_43_out);
  not not_43 (not_43_out, Op[0]);
  buf ALU_Op_2 (ALU_Op[2], ori);  // OR_Gate
  // NOT_Gate not_44 is placed but not wired
  // NOT_Gate not_45 is placed but not wired
  buf ALU_Op_1 (ALU_Op[1], R);  // OR_Gate
  buf ALU_Op_0 (ALU_Op[0], beq);  // OR_Gate
  buf u_Shift_16bit (Shift_16bit, lui);  // OR_Gate
  buf u_J_L (J_L, jal);  // OR_Gate
  buf \H类  (HalfWord, lh);  // OR_Gate
  or \B类  (Byte, lb, sb);
  buf J_2 (J, j_t);  // OR_Gate

  // Notes on the sheet:
  //   0读取DM 1写入DM
  //   0Reg不写 1Reg写入
  //   0Alu写入Reg 1Mem写入Reg
  //   0Zero扩展 1Sign扩展
  //   0RT 1Extender
  //   0RT 1RD
  //   0不跳 1Branch
  //   000+  001-  010R  011^  100|
  //   0不左移 1左移
  //   0不跳 1J&L
  //   0Word 1HalfWord
  //   0Word 1Byte
endmodule

module _32bit_Adder (
  input  [31:0] A,
  input  [31:0] B,
  output [31:0] out_3
);

  Adder #(.width(32)) adder_1 (.a(A), .b(B), .out(out_3));  // open: cin, cout
endmodule

module _32bit_Subber (
  input  [31:0] A,
  input  [31:0] B,
  output [31:0] out_3
);

  Subtractor #(.width(32)) subtractor_1 (.a(A), .b(B), .out(out_3));  // open: bin, bout
endmodule

module _32bit_Andder (
  input  [31:0] A,
  input  [31:0] B,
  output [31:0] out_3
);

  assign out_3 = A & B;  // AND_Gate and_1, 32 bits wide
endmodule

module _32bit_Orer (
  input  [31:0] A,
  input  [31:0] B,
  output [31:0] out_3
);

  assign out_3 = A | B;  // OR_Gate or_1, 32 bits wide
endmodule

module _32bit_Comparer (
  input  [31:0] A,
  input  [31:0] B,
  output A_B,
  output A_B_2,
  output A_B_3
);

  Comparator #(.width(32)) comparator_1 (.a(A), .b(B), .gt(A_B), .eq(A_B_2), .lt(A_B_3));
endmodule

module ALU_Control (
  input  [2:0] ALU_Op,
  input  [5:0] Func,
  output [3:0] ALU_Ctr,
  output Jr
);

  wire Add_2_out, And_2_out, and_3_out, and_4_out, I_Add, I_Or, I_Sub, not_1_out, not_2_out, not_3_out,
       not_4_out, not_5_out, not_6_out, not_7_out, not_8_out, not_9_out, not_10_out, not_11_out, not_12_out,
       not_13_out, not_14_out, not_15_out, not_16_out, not_17_out, not_18_out, not_19_out, not_20_out,
       not_21_out, not_22_out, not_23_out, not_24_out, not_25_out, not_26_out, not_27_out, not_28_out,
       Or_2_out, Or_3_out, R, R_Add, R_And, R_Jr, R_Or, R_Sub, Sub_2_out;

  not not_1 (not_1_out, Func[4]);
  not not_2 (not_2_out, Func[3]);
  not not_3 (not_3_out, ALU_Op[0]);
  not not_4 (not_4_out, ALU_Op[1]);
  not not_5 (not_5_out, ALU_Op[2]);
  and \I加  (I_Add, not_5_out, not_4_out, not_3_out);
  not not_6 (not_6_out, Func[2]);
  not not_7 (not_7_out, Func[1]);
  and Add (R_Add, Func[5], not_1_out, not_2_out, not_6_out, not_7_out, Func[0]);
  not not_8 (not_8_out, ALU_Op[2]);
  not not_9 (not_9_out, ALU_Op[1]);
  and \I减  (I_Sub, not_8_out, ALU_Op[0]);
  not not_10 (not_10_out, Func[4]);
  not not_11 (not_11_out, ALU_Op[0]);
  not not_12 (not_12_out, ALU_Op[2]);
  and \R指令  (R, not_12_out, ALU_Op[1], not_11_out);
  not not_13 (not_13_out, Func[3]);
  not not_14 (not_14_out, Func[2]);
  and Sub (R_Sub, Func[5], not_10_out, not_13_out, not_14_out, Func[1], Func[0]);
  not not_15 (not_15_out, ALU_Op[1]);
  not not_16 (not_16_out, ALU_Op[0]);
  and \I或  (I_Or, ALU_Op[2], not_15_out, not_16_out);
  not not_17 (not_17_out, Func[4]);
  not not_18 (not_18_out, Func[3]);
  not not_19 (not_19_out, Func[1]);
  not not_20 (not_20_out, Func[0]);
  and And (R_And, Func[5], not_17_out, not_18_out, Func[2], not_19_out, not_20_out);
  not not_21 (not_21_out, Func[4]);
  not not_22 (not_22_out, Func[1]);
  not not_23 (not_23_out, Func[3]);
  and Or (R_Or, Func[5], not_21_out, not_23_out, Func[2], not_22_out, Func[0]);
  not not_24 (not_24_out, Func[2]);
  not not_25 (not_25_out, Func[4]);
  not not_26 (not_26_out, Func[5]);
  and u_Jr (R_Jr, not_26_out, not_25_out, Func[3], not_24_out, not_28_out, not_27_out);
  not not_27 (not_27_out, Func[0]);
  not not_28 (not_28_out, Func[1]);
  and And_2 (And_2_out, R, R_And);
  and Or_2 (Or_2_out, R, R_Or);
  and and_3 (and_3_out, R, R_Add);
  and and_4 (and_4_out, R, R_Sub);
  or Or_3 (Or_3_out, I_Or, Or_2_out);
  or Add_2 (Add_2_out, I_Add, and_3_out);
  or Sub_2 (Sub_2_out, I_Sub, and_4_out);
  buf _3 (ALU_Ctr[3], 1'b0);  // OR_Gate
  or _2 (ALU_Ctr[2], 1'b0, Sub_2_out);
  or _1 (ALU_Ctr[1], 1'b0, Add_2_out, Sub_2_out);
  and and_5 (Jr, R_Jr, R);
  or _0 (ALU_Ctr[0], 1'b0, Or_3_out);
endmodule

module _16bit_ControlToNumber (
  input  _0000,
  input  _0001,
  input  _0010,
  input  _0011,
  input  _0100,
  input  _0101,
  input  _0110,
  input  _0111,
  input  _1000,
  input  _1001,
  input  _1010,
  input  _1011,
  input  _1100,
  input  _1101,
  input  _1110,
  input  _1111,
  output [3:0] ALU_Op
);

  assign ALU_Op = _0000 ? 4'b0000 : 4'bz;  // Controlled_Buffer controlled_buffer_1
  assign ALU_Op = _0001 ? 4'b0001 : 4'bz;  // Controlled_Buffer controlled_buffer_2
  assign ALU_Op = _0010 ? 4'b0010 : 4'bz;  // Controlled_Buffer controlled_buffer_3
  assign ALU_Op = _0011 ? 4'b0011 : 4'bz;  // Controlled_Buffer controlled_buffer_4
  assign ALU_Op = _0100 ? 4'b0100 : 4'bz;  // Controlled_Buffer controlled_buffer_5
  assign ALU_Op = _0101 ? 4'b0101 : 4'bz;  // Controlled_Buffer controlled_buffer_6
  assign ALU_Op = _0110 ? 4'b0110 : 4'bz;  // Controlled_Buffer controlled_buffer_7
  assign ALU_Op = _0111 ? 4'b0111 : 4'bz;  // Controlled_Buffer controlled_buffer_8
  assign ALU_Op = _1000 ? 4'b1000 : 4'bz;  // Controlled_Buffer controlled_buffer_9
  assign ALU_Op = _1001 ? 4'b1001 : 4'bz;  // Controlled_Buffer controlled_buffer_10
  assign ALU_Op = _1010 ? 4'b1010 : 4'bz;  // Controlled_Buffer controlled_buffer_11
  assign ALU_Op = _1011 ? 4'b1011 : 4'bz;  // Controlled_Buffer controlled_buffer_12
  assign ALU_Op = _1100 ? 4'b1100 : 4'bz;  // Controlled_Buffer controlled_buffer_13
  assign ALU_Op = _1101 ? 4'b1101 : 4'bz;  // Controlled_Buffer controlled_buffer_14
  assign ALU_Op = _1110 ? 4'b1110 : 4'bz;  // Controlled_Buffer controlled_buffer_15
  assign ALU_Op = _1111 ? 4'b1111 : 4'bz;  // Controlled_Buffer controlled_buffer_16
endmodule
