// Logisim project Mealy_FSM.circ as structural Verilog: 1 circuit, main circuit fsm
module fsm (
  input  [1:0] Input,
  input  Clr,
  output out_3
);

  wire _01_x0_out, _10_x0_2_out, _10_x0_out, and_1_out, and_2_out, clock_1_out, High_q, Low_q, not_1_out,
       not_2_out, not_3_out, not_4_out, not_5_out, not_6_out, not_7_out, not_8_out, not_9_out, not_10_out,
       or_1_out, or_2_out, register_1_q, xx_01_out;

  not not_1 (not_1_out, Input[0]);
  not not_2 (not_2_out, and_2_out);
  not not_3 (not_3_out, Input[0]);
  not not_4 (not_4_out, and_1_out);
  not not_5 (not_5_out, Input[0]);
  not not_6 (not_6_out, Input[1]);
  not not_7 (not_7_out, and_1_out);
  not not_8 (not_8_out, Input[0]);
  and _01_x0 (_01_x0_out, not_2_out, and_1_out, not_3_out);
  and _10_x0 (_10_x0_out, and_2_out, not_4_out, not_5_out);
  and xx_01 (xx_01_out, Input[0], not_6_out);
  and _10_x0_2 (_10_x0_2_out, and_2_out, not_7_out, not_8_out);
  Clock clock_1 (.out(clock_1_out));
  or or_1 (or_1_out, _01_x0_out, _10_x0_out);
  or or_2 (or_2_out, xx_01_out, _10_x0_2_out);
  Register #(.width(1)) High (.D(or_1_out), .Q(High_q), .clk(clock_1_out));  // open: en, clr
  Register #(.width(1)) Low (.D(or_2_out), .Q(Low_q), .clk(clock_1_out));  // open: en, clr
  Register #(.width(1)) register_1 (.D(Clr), .Q(register_1_q), .clk(clock_1_out));  // open: en, clr
  not not_9 (not_9_out, register_1_q);
  not not_10 (not_10_out, Low_q);
  and and_1 (and_1_out, not_9_out, Low_q);
  and and_2 (and_2_out, not_9_out, High_q);
  and and_3 (out_3, not_1_out, High_q, not_10_out);

  // Notes on the sheet:
  //   High
  //   Low
endmodule
