// Logisim project fibonacci_hard.circ as structural Verilog: 2 circuits, main circuit main
module main (
  input  [31:0] in_1,
  output [31:0] out_2
);

  wire and_1_out, clock_1_out, comparator_1_eq, comparator_2_gt, comparator_3_lt, counter_2_carry,
       multiplexer_1_out, or_1_out, register_1_q, register_2_q;
  wire [4:0] counter_2_q;
  wire [31:0] counter_1_q, counter_3_q, counter_4_q, multiplexer_2_out, multiplexer_3_out, multiplexer_4_out,
       multiplexer_5_out, multiplexer_6_out, multiplexer_7_out, multiplexer_8_out, multiplexer_9_out,
       n4x4_matrix_mult_1_out_9, n4x4_matrix_mult_1_out_10, n4x4_matrix_mult_1_out_11,
       n4x4_matrix_mult_1_out_12, n4x4_matrix_mult_2_out_9, n4x4_matrix_mult_2_out_10,
       n4x4_matrix_mult_2_out_11, n4x4_matrix_mult_2_out_12, register_3_q, register_4_q, register_5_q,
       register_6_q, register_7_q, register_8_q, register_9_q, register_10_q;

  Counter #(.width(32), .max('hffffffff)) counter_1 (
    .Q(counter_1_q), .clk(clock_1_out));  // open: load, D, count, carry, clr
  Comparator #(.width(32), .mode("unsigned")) comparator_1 (
    .a(counter_1_q), .b(32'h1), .eq(comparator_1_eq));  // open: gt, lt
  Multiplexer #(.select(5)) multiplexer_1 (
    .in0(in_1[0]), .in1(in_1[1]), .in2(in_1[2]), .in3(in_1[3]), .in4(in_1[4]), .in5(in_1[5]), .in6(in_1[6]),
    .in7(in_1[7]), .in8(in_1[8]), .in9(in_1[9]), .in10(in_1[10]), .in11(in_1[11]), .in12(in_1[12]),
    .in13(in_1[13]), .in14(in_1[14]), .in15(in_1[15]), .in16(in_1[16]), .in17(in_1[17]), .in18(in_1[18]),
    .in19(in_1[19]), .in20(in_1[20]), .in21(in_1[21]), .in22(in_1[22]), .in23(in_1[23]), .in24(in_1[24]),
    .in25(in_1[25]), .in26(in_1[26]), .in27(in_1[27]), .in28(in_1[28]), .in29(in_1[29]), .in30(in_1[30]),
    .in31(in_1[31]), .out(multiplexer_1_out), .sel(counter_2_q));  // open: en
  Multiplexer #(.width(32)) multiplexer_2 (
    .in0(n4x4_matrix_mult_1_out_9), .in1(32'h1), .out(multiplexer_2_out), .sel(comparator_1_eq));  // open: en
  Multiplexer #(.width(32)) multiplexer_3 (
    .in0(n4x4_matrix_mult_1_out_10), .in1(32'h1), .out(multiplexer_3_out), .sel(comparator_1_eq));  // open: en
  Multiplexer #(.width(32)) multiplexer_4 (
    .in0(n4x4_matrix_mult_1_out_11), .in1(32'h1), .out(multiplexer_4_out), .sel(comparator_1_eq));  // open: en
  Multiplexer #(.width(32)) multiplexer_5 (
    .in0(n4x4_matrix_mult_1_out_12), .out(multiplexer_5_out), .sel(comparator_1_eq));  // open: in1, en
  Clock clock_1 (.out(clock_1_out));
  and and_1 (and_1_out, multiplexer_1_out, comparator_2_gt);
  Register #(.width(1)) register_1 (.D(and_1_out), .Q(register_1_q), .clk(clock_1_out));  // open: en, clr
  Counter #(.width(5), .max('h1f)) counter_2 (
    .Q(counter_2_q), .carry(counter_2_carry), .clk(clock_1_out));  // open: load, D, count, clr
  Register #(.width(1)) register_2 (.D(register_1_q), .Q(register_2_q), .clk(clock_1_out));  // open: en, clr
  or or_1 (or_1_out, register_2_q, comparator_1_eq);
  Register #(.width(32)) register_3 (.D(multiplexer_2_out), .Q(register_3_q), .clk(clock_1_out));  // open: en, clr
  Register #(.width(32)) register_4 (.D(multiplexer_3_out), .Q(register_4_q), .clk(clock_1_out));  // open: en, clr
  Register #(.width(32)) register_5 (.D(multiplexer_4_out), .Q(register_5_q), .clk(clock_1_out));  // open: en, clr
  Register #(.width(32)) register_6 (.D(multiplexer_5_out), .Q(register_6_q), .clk(clock_1_out));  // open: en, clr
  Multiplexer #(.width(32)) multiplexer_6 (
    .in0(n4x4_matrix_mult_2_out_10), .out(multiplexer_6_out), .sel(comparator_1_eq));  // open: in1, en
  Multiplexer #(.width(32)) multiplexer_7 (
    .in0(n4x4_matrix_mult_2_out_11), .in1(32'h1), .out(multiplexer_7_out), .sel(comparator_1_eq));  // open: en
  Multiplexer #(.width(32)) multiplexer_8 (
    .in0(n4x4_matrix_mult_2_out_12), .out(multiplexer_8_out), .sel(comparator_1_eq));  // open: in1, en
  Comparator #(.width(32), .mode("unsigned")) comparator_2 (
    .a(32'h1), .b(counter_3_q), .gt(comparator_2_gt));  // open: eq, lt
  Counter #(.width(32), .max('hffffffff)) counter_3 (
    .count(counter_2_carry), .Q(counter_3_q), .clk(clock_1_out));  // open: load, D, carry, clr
  _4x4_Matrix_Mult u_4x4_matrix_mult_1 (
    .in_1(register_3_q), .in_2(register_4_q), .in_3(register_5_q), .in_4(register_6_q), .in_5(register_3_q),
    .in_6(register_4_q), .in_7(register_5_q), .in_8(register_6_q), .out_9(n4x4_matrix_mult_1_out_9),
    .out_10(n4x4_matrix_mult_1_out_10), .out_11(n4x4_matrix_mult_1_out_11), .out_12(n4x4_matrix_mult_1_out_12));
  Multiplexer #(.width(32)) multiplexer_9 (
    .in0(n4x4_matrix_mult_2_out_9), .in1(32'h1), .out(multiplexer_9_out), .sel(comparator_1_eq));  // open: en
  Register #(.width(32)) register_7 (
    .D(multiplexer_9_out), .en(or_1_out), .Q(register_7_q), .clk(clock_1_out));  // open: clr
  Register #(.width(32)) register_8 (
    .D(multiplexer_6_out), .en(or_1_out), .Q(register_8_q), .clk(clock_1_out));  // open: clr
  Register #(.width(32)) register_9 (
    .D(multiplexer_7_out), .en(or_1_out), .Q(register_9_q), .clk(clock_1_out));  // open: clr
  Register #(.width(32)) register_10 (
    .D(multiplexer_8_out), .en(or_1_out), .Q(register_10_q), .clk(clock_1_out));  // open: clr
  _4x4_Matrix_Mult u_4x4_matrix_mult_2 (
    .in_1(register_7_q), .in_2(register_8_q), .in_3(register_9_q), .in_4(register_10_q), .in_5(register_3_q),
    .in_6(register_4_q), .in_7(register_5_q), .in_8(register_6_q), .out_9(n4x4_matrix_mult_2_out_9),
    .out_10(n4x4_matrix_mult_2_out_10), .out_11(n4x4_matrix_mult_2_out_11), .out_12(n4x4_matrix_mult_2_out_12));
  Counter #(.width(32), .max('hffffffff)) counter_4 (
    .Q(counter_4_q), .clk(clock_1_out));  // open: load, D, count, carry, clr
  Comparator #(.width(32), .mode("unsigned")) comparator_3 (
    .a(32'h32), .b(counter_4_q), .lt(comparator_3_lt));  // open: gt, eq
  Register #(.width(32)) register_11 (
    .D(register_8_q), .en(comparator_3_lt), .Q(out_2), .clk(clock_1_out));  // open: clr
endmodule

module _4x4_Matrix_Mult (
  input  [31:0] in_1,
  input  [31:0] in_2,
  input  [31:0] in_3,
  input  [31:0] in_4,
  input  [31:0] in_5,
  input  [31:0] in_6,
  input  [31:0] in_7,
  input  [31:0] in_8,
  output [31:0] out_9,
  output [31:0] out_10,
  output [31:0] out_11,
  output [31:0] out_12
);

  wire [31:0] multiplier_1_out, multiplier_2_out, multiplier_3_out, multiplier_4_out, multiplier_5_out,
       multiplier_6_out, multiplier_7_out, multiplier_8_out;

  Multiplier #(.width(32)) multiplier_1 (.a(in_1), .b(in_5), .out(multiplier_1_out));  // open: cin, cout
  Multiplier #(.width(32)) multiplier_2 (.a(in_2), .b(in_7), .out(multiplier_2_out));  // open: cin, cout
  Multiplier #(.width(32)) multiplier_3 (.a(in_1), .b(in_6), .out(multiplier_3_out));  // open: cin, cout
  Multiplier #(.width(32)) multiplier_4 (.a(in_2), .b(in_8), .out(multiplier_4_out));  // open: cin, cout
  Multiplier #(.width(32)) multiplier_5 (.a(in_3), .b(in_5), .out(multiplier_5_out));  // open: cin, cout
  Multiplier #(.width(32)) multiplier_6 (.a(in_4), .b(in_7), .out(multiplier_6_out));  // open: cin, cout
  Multiplier #(.width(32)) multiplier_7 (.a(in_3), .b(in_6), .out(multiplier_7_out));  // open: cin, cout
  Multiplier #(.width(32)) multiplier_8 (.a(in_4), .b(in_8), .out(multiplier_8_out));  // open: cin, cout
  Adder #(.width(32)) adder_1 (.a(multiplier_1_out), .b(multiplier_2_out), .out(out_9));  // open: cin, cout
  Adder #(.width(32)) adder_2 (.a(multiplier_3_out), .b(multiplier_4_out), .out(out_10));  // open: cin, cout
  Adder #(.width(32)) adder_3 (.a(multiplier_5_out), .b(multiplier_6_out), .out(out_11));  // open: cin, cout
  Adder #(.width(32)) adder_4 (.a(multiplier_7_out), .b(multiplier_8_out), .out(out_12));  // open: cin, cout
endmodule
