// Logisim project 自组64_8CPU.circ as structural Verilog: 1 circuit, main circuit main
module main (
  input  [12:0] Address,
  input  MREQ,
  input  [2:0] in_3,
  input  WR,
  input  [7:0] Input,
  output [7:0] Output
);

  wire _74138_out, and_1_out, and_2_out, and_3_out, and_4_out, and_5_out, and_6_out, and_7_out, and_8_out,
       clock_1_out, decoder_1_out0, decoder_1_out1, decoder_1_out2, decoder_1_out3, decoder_1_out4,
       decoder_1_out5, decoder_1_out6, decoder_1_out7, not_1_out, not_2_out, not_3_out, not_4_out, not_5_out,
       not_6_out, not_7_out, not_8_out, not_9_out, not_10_out, not_11_out, not_12_out, not_13_out,
       not_14_out, not_15_out, not_16_out;
  wire [7:0] controlled_buffer_1_out;

  not _74138 (_74138_out, decoder_1_out0);
  not not_1 (not_1_out, decoder_1_out1);
  not not_2 (not_2_out, decoder_1_out2);
  not not_3 (not_3_out, decoder_1_out3);
  not not_4 (not_4_out, decoder_1_out4);
  not not_5 (not_5_out, decoder_1_out5);
  not not_6 (not_6_out, decoder_1_out6);
  not not_7 (not_7_out, decoder_1_out7);
  Decoder #(.select(3)) decoder_1 (
    .out0(decoder_1_out0), .out1(decoder_1_out1), .out2(decoder_1_out2), .out3(decoder_1_out3),
    .out4(decoder_1_out4), .out5(decoder_1_out5), .out6(decoder_1_out6), .out7(decoder_1_out7), .sel(in_3));  // open: en
  not not_8 (not_8_out, _74138_out);
  not not_9 (not_9_out, not_1_out);
  not not_10 (not_10_out, not_2_out);
  not not_11 (not_11_out, not_3_out);
  not not_12 (not_12_out, not_4_out);
  not not_13 (not_13_out, not_5_out);
  not not_14 (not_14_out, not_6_out);
  not not_15 (not_15_out, not_7_out);
  and and_1 (and_1_out, not_8_out, MREQ);
  and and_2 (and_2_out, not_9_out, MREQ);
  and and_3 (and_3_out, not_10_out, MREQ);
  and and_4 (and_4_out, not_11_out, MREQ);
  and and_5 (and_5_out, not_12_out, MREQ);
  and and_6 (and_6_out, not_13_out, MREQ);
  and and_7 (and_7_out, not_14_out, MREQ);
  and and_8 (and_8_out, not_15_out, MREQ);
  Clock clock_1 (.out(clock_1_out));
  not not_16 (not_16_out, WR);
  assign controlled_buffer_1_out = not_16_out ? Input : 8'bz;  // Controlled_Buffer controlled_buffer_1
  RAM #(.addrWidth(13)) ram_1 (
    .addr(Address), .data(controlled_buffer_1_out), .sel(and_1_out), .clk(clock_1_out), .ld(WR));  // open: clr
  RAM #(.addrWidth(13)) ram_2 (
    .addr(Address), .data(controlled_buffer_1_out), .sel(and_2_out), .clk(clock_1_out), .ld(WR));  // open: clr
  RAM #(.addrWidth(13)) ram_3 (
    .addr(Address), .data(controlled_buffer_1_out), .sel(and_3_out), .clk(clock_1_out), .ld(WR));  // open: clr
  RAM #(.addrWidth(13)) ram_4 (
    .addr(Address), .data(controlled_buffer_1_out), .sel(and_4_out), .clk(clock_1_out), .ld(WR));  // open: clr
  RAM #(.addrWidth(13)) ram_5 (
    .addr(Address), .data(controlled_buffer_1_out), .sel(and_5_out), .clk(clock_1_out), .ld(WR));  // open: clr
  RAM #(.addrWidth(13)) ram_6 (
    .addr(Address), .data(controlled_buffer_1_out), .sel(and_6_out), .clk(clock_1_out), .ld(WR));  // open: clr
  RAM #(.addrWidth(13)) ram_7 (
    .addr(Address), .data(controlled_buffer_1_out), .sel(and_7_out), .clk(clock_1_out), .ld(WR));  // open: clr
  RAM #(.addrWidth(13)) ram_8 (
    .addr(Address), .data(controlled_buffer_1_out), .sel(and_8_out), .clk(clock_1_out), .ld(WR));  // open: clr
  assign Output = WR ? controlled_buffer_1_out : 8'bz;  // Controlled_Buffer controlled_buffer_2

  // Notes on the sheet:
  //   A
  //   B
  //   C
  //   D
  //   E
  //   F
  //   G
  //   H
  //   DataBus
endmodule
